# Fritzing sketch Ses kontrollü müzik çalar (saved by Fritzing 0.8.7b)
breadboards: 1

parts:
  Eleman1 = Arduino Uno (Rev3)
  sdCard1 = my_sdCard
  Eleman2 = Bluetooth HC-06 Macho  # not connected
  R1 = Resistor [tolerance=±5% resistance=220 package=THT]
  R2 = Resistor [tolerance=±5% resistance=220 package=THT]
  R3 = Resistor [tolerance=±5% resistance=220 package=THT]
  SP1 = SPEAKER [package=pcb_mount_speaker]

nets:
  N1: Eleman1.D9_PWM, SP1.+
  N2: Eleman1.D11_PWM/MOSI, sdCard1.MOSI
  N3: Eleman1.D12/MISO, sdCard1.MISO
  N4: Eleman1.D13/SCK, sdCard1.SCK
  N5: Eleman1.D4, sdCard1.CS
  N6: Eleman1.D6_PWM, R1.Pin_0
  5V: Eleman1.5V, sdCard1.VCC
  GND: Eleman1.GND, sdCard1.GND, R3.Pin_1, SP1.-
  N7: R1.Pin_1, R2.Pin_0
  N8: R2.Pin_1, R3.Pin_0

custom parts:
  my_sdCard: micro sdCard Adapter with 90º pin header. Use a filtering Capacitor between CS and GND if needed. PCB View Pinouts are Reversed for laying parallel on PCB using a 90º pin header.
